// Logisim project led7seg.circ as structural Verilog
module led7b (
  input  x,
  input  y,
  input  w,
  input  z,
  output a,
  output b,
  output c,
  output d,
  output e,
  output f,
  output g
);

  wire and_1_out, and_2_out, and_3_out, and_4_out, and_5_out, and_6_out, and_7_out, and_8_out, and_9_out,
       and_10_out, and_11_out, and_12_out, and_13_out, and_14_out, and_15_out, and_16_out, and_17_out,
       and_18_out, and_19_out, and_20_out, and_21_out, and_22_out, and_23_out, and_24_out, and_25_out,
       and_26_out, not_1_out, not_2_out, not_3_out, not_4_out;

  not not_1 (not_1_out, x);
  not not_2 (not_2_out, y);
  not not_3 (not_3_out, w);
  not not_4 (not_4_out, z);
  and and_1 (and_1_out, y, not_4_out);
  and and_2 (and_2_out, not_2_out, not_3_out, z);
  and and_3 (and_3_out, x, w, not_4_out);
  and and_4 (and_4_out, not_1_out, not_2_out, not_3_out);
  and and_5 (and_5_out, not_2_out, not_3_out);
  and and_6 (and_6_out, not_1_out, not_2_out, not_4_out);
  and and_7 (and_7_out, not_3_out, not_4_out);
  and and_8 (and_8_out, x, y, not_4_out);
  and and_9 (and_9_out, not_2_out, not_3_out);
  and and_10 (and_10_out, w, not_4_out);
  and and_11 (and_11_out, x, not_4_out);
  and and_12 (and_12_out, not_1_out, y, not_4_out);
  and and_13 (and_13_out, not_2_out, not_3_out, z);
  and and_14 (and_14_out, x, not_2_out, w, not_4_out);
  and and_15 (and_15_out, y, not_3_out, not_4_out);
  and and_16 (and_16_out, not_1_out, not_2_out, not_3_out);
  and and_17 (and_17_out, not_1_out, not_2_out, not_3_out);
  and and_18 (and_18_out, not_1_out, y, not_4_out);
  and and_19 (and_19_out, not_1_out, w, not_4_out);
  and and_20 (and_20_out, not_2_out, not_3_out, z);
  and and_21 (and_21_out, not_2_out, w, not_4_out);
  and and_22 (and_22_out, not_1_out, not_2_out, not_3_out);
  and and_23 (and_23_out, not_2_out, not_3_out, z);
  and and_24 (and_24_out, not_2_out, w, not_4_out);
  and and_25 (and_25_out, y, not_3_out, not_4_out);
  and and_26 (and_26_out, not_1_out, w, not_4_out);
  or or_1 (a, and_1_out, and_2_out, and_3_out, and_4_out);
  or or_2 (b, and_5_out, and_6_out, and_7_out, and_8_out);
  or or_3 (c, and_9_out, and_10_out, and_11_out);
  or or_4 (d, and_12_out, and_13_out, and_14_out, and_15_out, and_16_out);
  or or_5 (e, and_17_out, and_18_out);
  or or_6 (f, and_19_out, and_20_out, and_21_out, and_22_out);
  or or_7 (g, and_23_out, and_24_out, and_25_out, and_26_out);
  _7_Segment_Display u_7_segment_display_1 (.g(g), .f(f), .a(a), .b(b), .e(e), .d(d), .c(c));  // open: dp
endmodule

module testeconversor (
  input  [3:0] in_1,
  input  [3:0] in_2,
  output adec,
  output bdec,
  output cdec,
  output ddec,
  output edec,
  output fdec,
  output gdec,
  output auni,
  output buni,
  output cuni,
  output duni,
  output euni,
  output funi,
  output guni
);

  led7b led7b_1 (
    .x(in_1[0]), .y(in_1[1]), .w(in_1[2]), .z(in_1[3]), .a(adec), .b(bdec), .c(cdec), .d(ddec), .e(edec),
    .f(fdec), .g(gdec));
  led7b led7b_2 (
    .x(in_2[0]), .y(in_2[1]), .w(in_2[2]), .z(in_2[3]), .a(auni), .b(buni), .c(cuni), .d(duni), .e(euni),
    .f(funi), .g(guni));
endmodule

module novoteste (
  input  [3:0] decimal,
  input  [3:0] unidade
);

  wire testeconversor_1_adec, testeconversor_1_auni, testeconversor_1_bdec, testeconversor_1_buni,
       testeconversor_1_cdec, testeconversor_1_cuni, testeconversor_1_ddec, testeconversor_1_duni,
       testeconversor_1_edec, testeconversor_1_euni, testeconversor_1_fdec, testeconversor_1_funi,
       testeconversor_1_gdec, testeconversor_1_guni;

  testeconversor testeconversor_1 (
    .in_1(decimal), .in_2(unidade), .adec(testeconversor_1_adec), .bdec(testeconversor_1_bdec),
    .cdec(testeconversor_1_cdec), .ddec(testeconversor_1_ddec), .edec(testeconversor_1_edec),
    .fdec(testeconversor_1_fdec), .gdec(testeconversor_1_gdec), .auni(testeconversor_1_auni),
    .buni(testeconversor_1_buni), .cuni(testeconversor_1_cuni), .duni(testeconversor_1_duni),
    .euni(testeconversor_1_euni), .funi(testeconversor_1_funi), .guni(testeconversor_1_guni));
  _7_Segment_Display u_7_segment_display_1 (
    .g(testeconversor_1_gdec), .f(testeconversor_1_fdec), .a(testeconversor_1_adec),
    .b(testeconversor_1_bdec), .e(testeconversor_1_edec), .d(testeconversor_1_ddec), .c(testeconversor_1_cdec));  // open: dp
  _7_Segment_Display u_7_segment_display_2 (
    .g(testeconversor_1_guni), .f(testeconversor_1_funi), .a(testeconversor_1_auni),
    .b(testeconversor_1_buni), .e(testeconversor_1_euni), .d(testeconversor_1_duni), .c(testeconversor_1_cuni));  // open: dp
endmodule

module subtrador (
  input  [6:0] in_1
);

  wire subtractor_1_bout, undriven;
  wire [6:0] multiplexer_1_out, negator_1_out, subtractor_1_out;

  Subtractor #(.width(7)) subtractor_1 (
    .a(in_1), .b(7'b0110010), .out(subtractor_1_out), .bin(undriven), .bout(subtractor_1_bout));
  Multiplexer #(.width(7)) multiplexer_1 (
    .in0(subtractor_1_out), .in1(negator_1_out), .out(multiplexer_1_out), .sel(subtractor_1_bout));
  Negator #(.width(7)) negator_1 (.in(subtractor_1_out), .out(negator_1_out));
endmodule
